// Digital circuit trabalho sd.dig as structural Verilog
module trabalho_sd (
  input  A,
  input  C,
  input  B,
  output R0,
  output R1
);

  wire xor_1_out;

  xor xor_1 (xor_1_out, B, A);
  xor xor_2 (R0, C, xor_1_out);
  Multiplexer #(.Selector_Bits(2)) multiplexer_1 (.sel({B, C}), .in_0(1'b0), .in_1(A), .in_2(A), .in_3(1'b1), .out(R1));
endmodule

/* Test case:
A B C R1 R0 

 0 0 0 0 0
 0 0 1 0 1
 0 1 0 0 1
 0 1 1 1 0
 1 0 0 0 1
 1 0 1 1 0
 1 1 0 1 0
 1 1 1 1 1
*/
